// Logisim project devoir_1_c_1227.circ as structural Verilog: 1 circuit, main circuit main
module main (
  input  E,
  input  [3:0] ABCD,
  output out_3,
  output out_4
);

  wire decoder_1_out3, decoder_1_out11, decoder_1_out13, decoder_1_out14, decoder_1_out15, or_1_out, or_2_out;

  Decoder #(.select(4)) decoder_1 (
    .out3(decoder_1_out3), .out11(decoder_1_out11), .out13(decoder_1_out13), .out14(decoder_1_out14),
    .out15(decoder_1_out15), .sel(ABCD));  // open: out0, out1, out2, out4, out5, out6, out7, out8, out9, out10, out12, en
  buf or_1 (or_1_out, decoder_1_out3);  // OR_Gate
  or or_2 (or_2_out, decoder_1_out11, decoder_1_out13, decoder_1_out14, decoder_1_out15);
  or or_3 (out_4, or_1_out, or_2_out);
  not not_1 (out_3, out_4);
endmodule
